// Logisim project processor.circ as structural Verilog: 2 circuits, main circuit main
module main (
  input  manual_reset,
  input  in_2
);

  wire ADD, and_1_out, and_3_out, and_4_out, and_5_out, and_6_out, and_8_out, and_9_out, and_10_out,
       and_11_out, and_12_out, and_13_out, and_14_out, and_15_out, and_16_out, and_17_out, and_19_out,
       and_20_out, and_21_out, and_22_out, and_23_out, and_24_out, and_25_out, and_26_out, and_27_out,
       and_28_out, and_29_out, and_30_out, and_31_out, and_32_out, and_33_out, and_34_out, and_35_out,
       and_36_out, and_37_out, and_38_out, and_39_out, and_40_out, and_41_out, and_42_out, and_43_out,
       and_44_out, and_45_out, and_46_out, and_47_out, and_48_out, and_49_out, and_50_out, and_51_out,
       and_52_out, and_53_out, and_54_out, and_55_out, and_56_out, and_57_out, and_58_out, and_59_out,
       and_60_out, and_61_out, and_62_out, and_63_out, and_64_out, and_65_out, and_66_out, and_67_out,
       and_68_out, and_69_out, and_70_out, and_71_out, and_72_out, and_73_out, and_74_out, and_75_out,
       and_76_out, and_77_out, B0eq1, CLK, Clock1_out, DE_I, EQ, GT, HALT, LT, nor_1_out, not_1_out,
       not_2_out, not_3_out, not_4_out, not_5_out, not_6_out, not_7_out, not_8_out, not_9_out, not_10_out,
       not_11_out, not_12_out, not_13_out, not_14_out, not_15_out, not_16_out, not_17_out, not_18_out,
       not_19_out, not_20_out, not_21_out, not_22_out, not_23_out, not_24_out, not_25_out, not_26_out,
       not_27_out, not_28_out, not_29_out, not_30_out, not_31_out, OPA_I, OPA_O, or_1_out, or_2_out,
       or_3_out, or_4_out, or_5_out, or_6_out, or_7_out, or_14_out, or_15_out, or_16_out, or_17_out,
       or_18_out, or_19_out, or_20_out, or_21_out, or_22_out, or_23_out, or_24_out, or_25_out, or_26_out,
       or_27_out, or_28_out, or_29_out, or_30_out, or_31_out, or_32_out, or_33_out, or_34_out, or_35_out,
       or_36_out, or_39_out, or_40_out, or_41_out, or_42_out, or_43_out, or_44_out, or_45_out, or_46_out,
       or_47_out, or_48_out, or_49_out, or_50_out, or_51_out, or_52_out, or_53_out, PC_I, PC_INC, PC_O,
       PRO_I, PRO_O, PRT, RA_I, RA_O, RAM_A, RAM_I, RAM_O, RB_I, RB_O, SL, SR, SUB, xor_1_out, xor_2_out,
       xor_3_out, xor_4_out, xor_5_out, xor_6_out, xor_7_out, xor_8_out, xor_9_out, xor_10_out, xor_11_out,
       xor_12_out, xor_13_out, xor_14_out, xor_15_out, xor_16_out;
  wire [0:0] or_54_out;
  wire [3:0] controlled_buffer_1_out, controlled_buffer_1_out_2;
  wire [7:0] ADDER_q, and_18_out, controlled_buffer_3_out, controlled_buffer_6_out, controlled_buffer_8_out,
       controlled_buffer_9_out, controlled_buffer_12_out, controlled_buffer_13_out, counter_1_q, hundos_data,
       non_binary_reg_1_o, non_binary_reg_3_debug, ones_data, or_38_out, Program_data, ram_1_dout,
       register_1_q, register_2_q, register_3_q, register_4_q, tens_data, xor_24_out;
  wire [7:1] non_binary_reg_4_debug;
  wire [7:4] undriven;

  ROM Program (.addr(non_binary_reg_1_o), .data(Program_data));
  not not_1 (not_1_out, HALT);
  or or_1 (or_1_out, manual_reset, and_1_out);
  and and_1 (and_1_out, counter_1_q[2], counter_1_q[0]);
  Clock Clock1 (.out(Clock1_out));
  and and_2 (CLK, Clock1_out, not_1_out);
  or or_2 (or_2_out, in_2, CLK);
  Counter counter_1 (
    .clr(or_1_out), .load(1'b0), .up(1'b1), .clk(not_2_out), .Q(counter_1_q));  // open: count, D, carry
  not not_2 (not_2_out, CLK);
  Register #(.trigger("high")) register_1 (
    .D({controlled_buffer_1_out_2, controlled_buffer_1_out}), .en(RAM_A), .clk(or_2_out), .Q(register_1_q),
    .clr(manual_reset));
  Register #(.trigger("high")) register_2 (
    .D({controlled_buffer_1_out_2, controlled_buffer_1_out}), .en(DE_I), .clk(CLK), .Q(register_2_q),
    .clr(or_1_out));
  non_binary_reg non_binary_reg_1 (
    .data_in({controlled_buffer_1_out_2, controlled_buffer_1_out}), .WE(PRO_I), .CLK(CLK), .OE(1'b1),
    .R(manual_reset), .O(non_binary_reg_1_o));  // open: DEBUG
  assign {controlled_buffer_1_out_2, controlled_buffer_1_out} = PRO_O ? Program_data : 8'bz;  // Controlled_Buffer controlled_buffer_1
  RAM ram_1 (
    .addr(register_1_q), .we(RAM_I), .oe(1'b1), .clk(or_2_out),
    .din({controlled_buffer_1_out_2, controlled_buffer_1_out}), .dout(ram_1_dout));
  non_binary_reg non_binary_reg_2 (
    .data_in({undriven, controlled_buffer_1_out}), .WE(OPA_I), .CLK(CLK), .OE(OPA_O), .R(manual_reset),
    .O({controlled_buffer_1_out_2, controlled_buffer_1_out}));  // open: DEBUG
  assign {controlled_buffer_1_out_2, controlled_buffer_1_out} = RAM_O ? ram_1_dout : 8'bz;  // Controlled_Buffer controlled_buffer_2
  Hex_Digit_Display hex_digit_display_1 (.value(controlled_buffer_1_out_2));  // open: dp
  Hex_Digit_Display hex_digit_display_2 (.value(controlled_buffer_1_out));  // open: dp
  ROM decoder_1 (
    .addr({register_2_q[7:4], counter_1_q[3:0]}), .data({PC_O, PC_INC, PC_I, PRO_I, PRO_O, DE_I, HALT, OPA_O}));
  ROM decoder_2 (
    .addr({register_2_q[7:4], counter_1_q[3:0]}), .data({OPA_I, RAM_O, RAM_I, RA_O, RA_I, RAM_A, RB_O, RB_I}));
  ROM decoder_3 (.addr({register_2_q[7:4], counter_1_q[3:0]}), .data({ADD, SUB, GT, LT, EQ, SL, SR, PRT}));
  and and_3 (and_3_out, B0eq1, PC_I);
  assign controlled_buffer_3_out = RB_I ? {controlled_buffer_1_out_2, controlled_buffer_1_out} : 8'bz;  // Controlled_Buffer controlled_buffer_3
  and and_4 (and_4_out, and_3_out, CLK);
  and and_5 (and_5_out, CLK, PC_INC);
  Register #(.trigger("high")) register_3 (
    .D({controlled_buffer_1_out_2, controlled_buffer_1_out}), .en(and_3_out), .clk(CLK), .Q(register_3_q),
    .clr(manual_reset));
  assign controlled_buffer_3_out = or_5_out ? or_38_out : 8'bz;  // Controlled_Buffer controlled_buffer_4
  or or_3 (or_3_out, RB_I, or_5_out);
  or or_4 (or_4_out, and_4_out, and_5_out);
  Counter ADDER (
    .clr(manual_reset), .load(and_4_out), .up(1'b1), .clk(or_4_out), .D(register_3_q), .Q(ADDER_q));  // open: count, carry
  non_binary_reg non_binary_reg_3 (
    .data_in({controlled_buffer_1_out_2, controlled_buffer_1_out}), .WE(RA_I), .CLK(CLK), .OE(RA_O),
    .R(manual_reset), .O({controlled_buffer_1_out_2, controlled_buffer_1_out}), .DEBUG(non_binary_reg_3_debug));
  or or_5 (or_5_out, ADD, SUB, SR, SL, LT, EQ, GT);
  non_binary_reg non_binary_reg_4 (
    .data_in(controlled_buffer_3_out), .WE(or_3_out), .CLK(CLK), .OE(RB_O), .R(manual_reset),
    .O({controlled_buffer_1_out_2, controlled_buffer_1_out}), .DEBUG({non_binary_reg_4_debug, B0eq1}));
  assign {controlled_buffer_1_out_2, controlled_buffer_1_out} = PC_O ? ADDER_q : 8'bz;  // Controlled_Buffer controlled_buffer_5
  Register register_4 (.D({non_binary_reg_4_debug, B0eq1}), .en(PRT), .clk(CLK), .Q(register_4_q), .clr(manual_reset));
  ROM ones (.addr(register_4_q), .data(ones_data));
  ROM tens (.addr(register_4_q), .data(tens_data));
  ROM hundos (.addr(register_4_q), .data(hundos_data));
  _7_Segment_Display u_7_segment_display_1 (
    .g(hundos_data[3]), .f(hundos_data[2]), .a(hundos_data[1]), .b(hundos_data[0]), .e(hundos_data[4]),
    .d(hundos_data[5]), .c(hundos_data[6]), .dp(hundos_data[7]));
  _7_Segment_Display u_7_segment_display_2 (
    .g(tens_data[3]), .f(tens_data[2]), .a(tens_data[1]), .b(tens_data[0]), .e(tens_data[4]),
    .d(tens_data[5]), .c(tens_data[6]), .dp(tens_data[7]));
  or or_6 (or_6_out, SL, SR);
  _7_Segment_Display u_7_segment_display_3 (
    .g(ones_data[3]), .f(ones_data[2]), .a(ones_data[1]), .b(ones_data[0]), .e(ones_data[4]),
    .d(ones_data[5]), .c(ones_data[6]), .dp(ones_data[7]));
  assign controlled_buffer_6_out = or_6_out ? non_binary_reg_3_debug : 8'bz;  // Controlled_Buffer controlled_buffer_6
  not not_3 (not_3_out, or_6_out);
  assign controlled_buffer_6_out = not_3_out ? {8{1'b0}} : 8'bz;  // Controlled_Buffer controlled_buffer_7
  or or_7 (or_7_out, ADD, SUB);
  assign controlled_buffer_8_out = or_7_out ? non_binary_reg_3_debug : 8'bz;  // Controlled_Buffer controlled_buffer_8
  assign controlled_buffer_9_out = or_7_out ? {controlled_buffer_1_out_2, controlled_buffer_1_out} : 8'bz;  // Controlled_Buffer controlled_buffer_9
  assign controlled_buffer_8_out = not_4_out ? {8{1'b0}} : 8'bz;  // Controlled_Buffer controlled_buffer_10
  not not_4 (not_4_out, or_7_out);
  not not_5 (not_5_out, or_7_out);
  assign controlled_buffer_9_out = not_5_out ? {8{1'b0}} : 8'bz;  // Controlled_Buffer controlled_buffer_11
  not not_6 (not_6_out, SR);
  xor xor_1 (xor_1_out, SUB, controlled_buffer_9_out[7]);
  xor xor_2 (xor_2_out, SUB, controlled_buffer_9_out[5]);
  xor xor_3 (xor_3_out, SUB, controlled_buffer_9_out[3]);
  xor xor_4 (xor_4_out, SUB, controlled_buffer_9_out[1]);
  and and_6 (and_6_out, SR, controlled_buffer_6_out[7]);
  and and_7 (and_18_out[7], not_6_out, controlled_buffer_6_out[6]);
  and and_8 (and_8_out, controlled_buffer_6_out[6], SR);
  and and_9 (and_9_out, not_6_out, controlled_buffer_6_out[5]);
  and and_10 (and_10_out, controlled_buffer_6_out[5], SR);
  and and_11 (and_11_out, not_6_out, controlled_buffer_6_out[4]);
  and and_12 (and_12_out, controlled_buffer_6_out[4], SR);
  and and_13 (and_13_out, not_6_out, controlled_buffer_6_out[3]);
  and and_14 (and_14_out, controlled_buffer_6_out[3], SR);
  and and_15 (and_15_out, not_6_out, controlled_buffer_6_out[2]);
  and and_16 (and_16_out, controlled_buffer_6_out[2], SR);
  and and_17 (and_17_out, not_6_out, controlled_buffer_6_out[1]);
  and and_18 (and_18_out[0], controlled_buffer_6_out[1], SR);
  and and_19 (and_19_out, not_6_out, controlled_buffer_6_out[0]);
  xor xor_5 (xor_5_out, SUB, controlled_buffer_9_out[6]);
  xor xor_6 (xor_6_out, SUB, controlled_buffer_9_out[4]);
  xor xor_7 (xor_7_out, SUB, controlled_buffer_9_out[2]);
  xor xor_8 (xor_8_out, SUB, controlled_buffer_9_out[0]);
  or or_8 (and_18_out[6], and_6_out, and_9_out);
  or or_9 (and_18_out[5], and_8_out, and_11_out);
  or or_10 (and_18_out[4], and_10_out, and_13_out);
  or or_11 (and_18_out[3], and_12_out, and_15_out);
  or or_12 (and_18_out[2], and_14_out, and_17_out);
  or or_13 (and_18_out[1], and_16_out, and_19_out);
  or or_14 (or_14_out, LT, EQ, GT);
  and and_20 (and_20_out, controlled_buffer_8_out[7], xor_1_out);
  xor xor_9 (xor_9_out, controlled_buffer_8_out[7], xor_1_out);
  and and_21 (and_21_out, controlled_buffer_8_out[6], xor_5_out);
  xor xor_10 (xor_10_out, controlled_buffer_8_out[6], xor_5_out);
  and and_22 (and_22_out, controlled_buffer_8_out[5], xor_2_out);
  xor xor_11 (xor_11_out, controlled_buffer_8_out[5], xor_2_out);
  and and_23 (and_23_out, controlled_buffer_8_out[4], xor_6_out);
  xor xor_12 (xor_12_out, controlled_buffer_8_out[4], xor_6_out);
  and and_24 (and_24_out, controlled_buffer_8_out[3], xor_3_out);
  xor xor_13 (xor_13_out, controlled_buffer_8_out[3], xor_3_out);
  and and_25 (and_25_out, controlled_buffer_8_out[2], xor_7_out);
  xor xor_14 (xor_14_out, controlled_buffer_8_out[2], xor_7_out);
  and and_26 (and_26_out, controlled_buffer_8_out[1], xor_4_out);
  xor xor_15 (xor_15_out, controlled_buffer_8_out[1], xor_4_out);
  and and_27 (and_27_out, controlled_buffer_8_out[0], xor_8_out);
  xor xor_16 (xor_16_out, controlled_buffer_8_out[0], xor_8_out);
  not not_7 (not_7_out, or_14_out);
  assign controlled_buffer_12_out = or_14_out ? non_binary_reg_3_debug : 8'bz;  // Controlled_Buffer controlled_buffer_12
  not not_8 (not_8_out, or_14_out);
  assign controlled_buffer_13_out = not_8_out ? {8{1'b0}} : 8'bz;  // Controlled_Buffer controlled_buffer_13
  assign controlled_buffer_13_out = or_14_out ? {controlled_buffer_1_out_2, controlled_buffer_1_out} : 8'bz;  // Controlled_Buffer controlled_buffer_14
  and and_28 (and_28_out, or_16_out, xor_9_out);
  and and_29 (and_29_out, or_17_out, xor_10_out);
  and and_30 (and_30_out, or_18_out, xor_11_out);
  and and_31 (and_31_out, or_19_out, xor_12_out);
  and and_32 (and_32_out, or_20_out, xor_13_out);
  and and_33 (and_33_out, or_21_out, xor_14_out);
  and and_34 (and_34_out, or_22_out, xor_15_out);
  and and_35 (and_35_out, SUB, xor_16_out);
  assign controlled_buffer_12_out = not_7_out ? {8{1'b0}} : 8'bz;  // Controlled_Buffer controlled_buffer_15
  or or_15 (or_15_out, and_20_out, and_28_out);
  xor xor_17 (xor_24_out[7], xor_9_out, or_16_out);
  or or_16 (or_16_out, and_21_out, and_29_out);
  xor xor_18 (xor_24_out[6], xor_10_out, or_17_out);
  or or_17 (or_17_out, and_22_out, and_30_out);
  xor xor_19 (xor_24_out[5], xor_11_out, or_18_out);
  or or_18 (or_18_out, and_23_out, and_31_out);
  xor xor_20 (xor_24_out[4], xor_12_out, or_19_out);
  or or_19 (or_19_out, and_24_out, and_32_out);
  xor xor_21 (xor_24_out[3], xor_13_out, or_20_out);
  or or_20 (or_20_out, and_25_out, and_33_out);
  xor xor_22 (xor_24_out[2], xor_14_out, or_21_out);
  or or_21 (or_21_out, and_26_out, and_34_out);
  xor xor_23 (xor_24_out[1], xor_15_out, or_22_out);
  or or_22 (or_22_out, and_27_out, and_35_out);
  xor xor_24 (xor_24_out[0], xor_16_out, SUB);
  LED led_1 (.in(or_15_out));
  not not_9 (not_9_out, controlled_buffer_12_out[7]);
  not not_10 (not_10_out, controlled_buffer_13_out[7]);
  not not_11 (not_11_out, controlled_buffer_12_out[6]);
  not not_12 (not_12_out, controlled_buffer_13_out[6]);
  not not_13 (not_13_out, controlled_buffer_12_out[5]);
  not not_14 (not_14_out, controlled_buffer_13_out[5]);
  not not_15 (not_15_out, controlled_buffer_12_out[4]);
  not not_16 (not_16_out, controlled_buffer_13_out[4]);
  not not_17 (not_17_out, controlled_buffer_12_out[3]);
  not not_18 (not_18_out, controlled_buffer_13_out[3]);
  not not_19 (not_19_out, controlled_buffer_12_out[2]);
  not not_20 (not_20_out, controlled_buffer_13_out[2]);
  not not_21 (not_21_out, controlled_buffer_12_out[1]);
  not not_22 (not_22_out, controlled_buffer_13_out[1]);
  not not_23 (not_23_out, controlled_buffer_12_out[0]);
  not not_24 (not_24_out, controlled_buffer_13_out[0]);
  and and_36 (and_36_out, not_9_out, controlled_buffer_13_out[7]);
  and and_37 (and_37_out, controlled_buffer_12_out[7], not_10_out);
  and and_38 (and_38_out, not_11_out, controlled_buffer_13_out[6]);
  and and_39 (and_39_out, controlled_buffer_12_out[6], not_12_out);
  and and_40 (and_40_out, not_13_out, controlled_buffer_13_out[5]);
  and and_41 (and_41_out, controlled_buffer_12_out[5], not_14_out);
  and and_42 (and_42_out, not_15_out, controlled_buffer_13_out[4]);
  and and_43 (and_43_out, controlled_buffer_12_out[4], not_16_out);
  and and_44 (and_44_out, not_17_out, controlled_buffer_13_out[3]);
  and and_45 (and_45_out, controlled_buffer_12_out[3], not_18_out);
  and and_46 (and_46_out, not_19_out, controlled_buffer_13_out[2]);
  and and_47 (and_47_out, controlled_buffer_12_out[2], not_20_out);
  and and_48 (and_48_out, not_21_out, controlled_buffer_13_out[1]);
  and and_49 (and_49_out, controlled_buffer_12_out[1], not_22_out);
  and and_50 (and_50_out, not_23_out, controlled_buffer_13_out[0]);
  and and_51 (and_51_out, controlled_buffer_12_out[0], not_24_out);
  or or_23 (or_23_out, and_36_out, and_37_out);
  not not_25 (not_25_out, or_23_out);
  or or_24 (or_24_out, and_38_out, and_39_out);
  not not_26 (not_26_out, or_31_out);
  or or_25 (or_25_out, and_40_out, and_41_out);
  not not_27 (not_27_out, or_32_out);
  or or_26 (or_26_out, and_42_out, and_43_out);
  not not_28 (not_28_out, or_33_out);
  or or_27 (or_27_out, and_44_out, and_45_out);
  not not_29 (not_29_out, or_34_out);
  or or_28 (or_28_out, and_46_out, and_47_out);
  not not_30 (not_30_out, or_35_out);
  or or_29 (or_29_out, and_48_out, and_49_out);
  not not_31 (not_31_out, or_36_out);
  or or_30 (or_30_out, and_50_out, and_51_out);
  and and_52 (and_52_out, not_25_out, or_24_out);
  or or_31 (or_31_out, and_52_out, or_23_out);
  and and_53 (and_53_out, not_26_out, or_25_out);
  or or_32 (or_32_out, and_53_out, or_31_out);
  and and_54 (and_54_out, not_27_out, or_26_out);
  or or_33 (or_33_out, and_54_out, or_32_out);
  and and_55 (and_55_out, not_28_out, or_27_out);
  or or_34 (or_34_out, and_55_out, or_33_out);
  and and_56 (and_56_out, not_29_out, or_28_out);
  or or_35 (or_35_out, and_56_out, or_34_out);
  and and_57 (and_57_out, not_30_out, or_29_out);
  or or_36 (or_36_out, and_57_out, or_35_out);
  and and_58 (and_58_out, not_31_out, or_30_out);
  // OR_Gate or_37 has open pins: in0=and_58_out, in1=or_36_out, out=open
  assign or_38_out = xor_24_out | and_18_out | {{7{1'b0}}, or_54_out[0]};  // OR_Gate or_38, 8 bits wide
  and and_59 (and_59_out, and_36_out, or_23_out);
  and and_60 (and_60_out, or_23_out, and_37_out);
  and and_61 (and_61_out, and_38_out, and_52_out);
  and and_62 (and_62_out, and_52_out, and_39_out);
  and and_63 (and_63_out, and_40_out, and_53_out);
  and and_64 (and_64_out, and_53_out, and_41_out);
  and and_65 (and_65_out, and_42_out, and_54_out);
  and and_66 (and_66_out, and_54_out, and_43_out);
  and and_67 (and_67_out, and_44_out, and_55_out);
  and and_68 (and_68_out, and_55_out, and_45_out);
  and and_69 (and_69_out, and_46_out, and_56_out);
  and and_70 (and_70_out, and_56_out, and_47_out);
  and and_71 (and_71_out, and_48_out, and_57_out);
  and and_72 (and_72_out, and_57_out, and_49_out);
  and and_73 (and_73_out, and_50_out, and_58_out);
  and and_74 (and_74_out, and_58_out, and_51_out);
  or or_39 (or_39_out, and_59_out, and_61_out);
  or or_40 (or_40_out, and_63_out, and_65_out);
  or or_41 (or_41_out, and_67_out, and_69_out);
  or or_42 (or_42_out, and_71_out, and_73_out);
  or or_43 (or_43_out, or_39_out, or_40_out);
  or or_44 (or_44_out, or_41_out, or_42_out);
  or or_45 (or_45_out, and_60_out, and_62_out);
  or or_46 (or_46_out, and_64_out, and_66_out);
  or or_47 (or_47_out, and_68_out, and_70_out);
  or or_48 (or_48_out, and_72_out, and_74_out);
  or or_49 (or_49_out, or_43_out, or_44_out);
  or or_50 (or_50_out, or_45_out, or_46_out);
  or or_51 (or_51_out, or_47_out, or_48_out);
  nor nor_1 (nor_1_out, or_49_out, or_52_out);
  or or_52 (or_52_out, or_50_out, or_51_out);
  and and_75 (and_75_out, EQ, nor_1_out);
  and and_76 (and_76_out, GT, or_52_out);
  and and_77 (and_77_out, LT, or_49_out);
  or or_53 (or_53_out, and_77_out, and_75_out);
  or or_54 (or_54_out[0], or_53_out, and_76_out);

  // Other names for the same wires on the sheet: RESET = manual_reset

  // Notes on the sheet:
  //   contents of Program (hex, n*v repeats v):
  //   0 40 20 41 21 10 51 e0 d0 31 c4
  //   RISC J processor
  //   contents of decoder_1 (hex, n*v repeats v):
  //   d0 c 2 15*0 1 15*0 1 15*0 1 15*0 1 15*0 1 15*0 1 15*0 1 15*0 1 15*0 1 15*0 1 15*0 1 15*0 21 20 14*0
  //   1
  //   contents of decoder_2 (hex, n*v repeats v):
  //   0 80 16*0 4 48 14*0 4 30 14*0 4 41 14*0 8 15*0 4 40 14*0 4 40 14*0 4 40 14*0 4 40 14*0 4 40 14*0 4
  //   40 14*0 4 40 30*0 4 22
  //   contents of decoder_3 (hex, n*v repeats v):
  //   83*0 80 15*0 40 15*0 10 15*0 20 15*0 8 15*0 4 15*0 2 46*0 1
  //   contents of ones (hex, n*v repeats v):
  //   77 41 3b 6b 4d 6e 7e 43 7f 6f 77 41 3b 6b 4d 6e 7e 43 7f 6f 77 41 3b 6b 4d 6e 7e 43 7f 6f 77 41 3b
  //   6b 4d 6e 7e 43 7f 6f 77 41 3b 6b 4d 6e 7e 43 7f 6f 77 41 3b 6b 4d 6e 7e 43 7f 6f 77 41 3b 6b 4d 6e
  //   7e 43 7f 6f 77 41 3b 6b 4d 6e 7e 43 7f 6f 77 41 3b 6b 4d 6e 7e 43 7f 6f 77 41 3b 6b 4d 6e 7e 43 7f
  //   6f 77 41 3b 6b 4d 6e 7e 43 7f 6f 77 41 3b 6b 4d 6e 7e 43 7f 6f 77 41 3b 6b 4d 6e 7e 43 7f 6f 77 41
  //   3b 6b 4d 6e 7e 43 7f 6f 77 41 3b 6b 4d 6e 7e 43 7f 6f 77 41 3b 6b 4d 6e 7e 43 7f 6f 77 41 3b 6b 4d
  //   6e 7e 43 7f 6f 77 41 3b 6b 4d 6e 7e 43 7f 6f 77 41 3b 6b 4d 6e 7e 43 7f 6f 77 41 3b 6b 4d 6e 7e 43
  //   7f 6f 77 41 3b 6b 4d 6e 7e 43 7f 6f 77 41 3b 6b 4d 6e 7e 43 7f 6f 77 41 3b 6b 4d 6e 7e 43 7f 6f 77
  //   41 3b 6b 4d 6e 7e 43 7f 6f 77 41 3b 6b 4d 6e 7e 43 7f 6f 77 41 3b 6b 4d 6e
  //   contents of tens (hex, n*v repeats v):
  //   10*77 10*41 10*3b 10*6b 10*4d 10*6e 10*7e 10*43 10*7f 10*6f 10*77 10*41 10*3b 10*6b 10*4d 10*6e
  //   10*7e 10*43 10*7f 10*6f 10*77 10*41 10*3b 10*6b 10*4d 6*6e
  //   contents of hundos (hex, n*v repeats v):
  //   100*77 100*41 56*3b
  //   NOTE: shift right loses 0, left loses 7
  //   A
  //   B
  //   C
  //   A
  //   B
  //   C
  //   A
  //   B
  //   C
  //   A
  //   B
  //   C
  //   A
  //   B
  //   C
  //   A
  //   B
  //   C
  //   A
  //   B
  //   C
  //   A
  //   B
  //   C
  //   C
  //   T
  //   C
  //   T
  //   C
  //   T
  //   C
  //   T
  //   C
  //   T
  //   C
  //   T
  //   C
  //   T
  //   C
  //   T
endmodule

module non_binary_reg (
  input  [7:0] data_in,
  input  WE,
  input  CLK,
  input  OE,
  input  R,
  output [7:0] O,
  output [7:0] DEBUG
);

  Register #(.trigger("high")) register_1 (.D(data_in), .en(WE), .clk(CLK), .Q(DEBUG), .clr(R));
  assign O = OE ? DEBUG : 8'bz;  // Controlled_Buffer controlled_buffer_1
endmodule
